// Logisim project both.circ as structural Verilog: 1 circuit, main circuit main
module main (
  input  in_1,
  input  in_2,
  input  in_3,
  input  in_4,
  input  in_5,
  input  in_6
);

  wire nand_1_out, nand_2_out, nand_3_out, nand_4_out, nand_5_out, nand_6_out, nand_7_out, nand_8_out,
       nand_9_out, not_1_out, not_2_out;

  not not_1 (not_1_out, in_1);
  not not_2 (not_2_out, in_2);
  nand nand_1 (nand_1_out, not_1_out, not_2_out, in_3);
  nand nand_2 (nand_2_out, not_1_out, in_2, in_4);
  nand nand_3 (nand_3_out, in_1, not_2_out, in_5);
  nand nand_4 (nand_4_out, in_1, in_2, in_6);
  nand nand_5 (nand_5_out, nand_9_out, not_2_out, not_1_out);
  nand nand_6 (nand_6_out, nand_9_out, not_2_out, in_1);
  nand nand_7 (nand_7_out, nand_9_out, in_2, not_1_out);
  nand nand_8 (nand_8_out, nand_9_out, in_2, in_1);
  nand nand_9 (nand_9_out, nand_1_out, nand_2_out, nand_3_out, nand_4_out);

  // Notes on the sheet:
  //   Selektor
  //   Selektor
  //   S
endmodule
