// Logisim project demiltiplexer.circ as structural Verilog: 1 circuit, main circuit main
module main (
  input  in_1,
  input  in_2,
  input  in_3
);

  wire nand_1_out, nand_2_out, nand_3_out, nand_4_out, not_1_out, not_2_out;

  not not_1 (not_1_out, in_1);
  not not_2 (not_2_out, in_2);
  nand nand_1 (nand_1_out, in_3, not_2_out, not_1_out);
  nand nand_2 (nand_2_out, in_3, not_2_out, in_1);
  nand nand_3 (nand_3_out, in_3, in_2, not_1_out);
  nand nand_4 (nand_4_out, in_3, in_2, in_1);

  // Notes on the sheet:
  //   Selektor
endmodule
